# Fritzing sketch Tiltroll (saved by Fritzing 0.7.5b)

parts:
  Part1 = Arduino XBee Shield
  MD03A1 = Dual VNH2SP30 Motor Driver [part_number=MD03A]
  M1 = DC Motor
  M2 = DC Motor
  VCC1 = Battery [part_number="Note should be 12 Volts"]
  Arduino1 = Arduino
  Part3 = IMU Analog Combo Board - 5 Degrees of Freedom
  U1 = Arduino Mega
  U2 = XBee  # not connected
  U3 = XBee  # not connected
  Part4 = XBee Explorer Regulated  # not connected
  S1 = Pushbutton [package="[THT]"]  # not connected
  S2 = Pushbutton [package="[THT]"]  # not connected

nets:
  N1: Part1.D_RX, Arduino1.D2
  N2: Part1.D_TX, Arduino1.D3, Part3.AZ
  N3: Part1.D4, Arduino1.D4
  N4: Part1.D5, Arduino1.D5
  N5: Part1.D6, Arduino1.D6
  N6: Part1.D7, Arduino1.D7
  N7: Part1.D8, Arduino1.D8
  N8: Part1.D9, Arduino1.D9
  N9: Part1.D10, Arduino1.D10
  N10: Part1.D11, Arduino1.D11
  N11: Part1.D12, Arduino1.D12
  N12: Part1.D13, Arduino1.D13
  5V: Part1.5V, Arduino1.+5V
  N13: Part1.A0, Part1.N$118, Arduino1.A0, Part3.XOUT
  N14: Part1.A1, Part1.N$106, Arduino1.A1, Part3.YOUT
  N15: Part1.A3, Part1.N$46, Arduino1.A3, Part3.XRATE
  N16: Part1.A4, Arduino1.A4
  N17: Part1.A5, Part1.N$58, Arduino1.A5, Part3.YRATE
  N18: Part1.AREF, Part1.N$70, Arduino1.aref, Part3.VREF
  GND: Part1.GND, Part1.N$33, VCC1.-, Arduino1.GND, Part3.GND
  N19: Part1.RST, Arduino1.RST
  N20: Part1.UART_RX, Arduino1.D0RX
  N21: Part1.UART_TX, Arduino1.D1TX
  VIN: Part1.VIN, VCC1.+, Arduino1.VIN
  3V3: Part1.N$21, Arduino1.3V3, Part3.3.3V
  N22: Part1.N$78, Part3.PTATS
  N23: Part1.N$82, Part3.ST
  N24: Part1.N$90, Part3.Y4.5OUT
  N25: Part1.N$94, Arduino1.A2, Part3.ZOUT
  N26: Part1.N$102, Part3.X4.5OUT
  N27: MD03A1.1INa, U1.D5
  N28: MD03A1.1INb, U1.D6
  N29: MD03A1.PWM, U1.D7
  N30: MD03A1.+5V_(IN), U1.+5V
  GND_2: MD03A1.GND, U1.GND
  VIN_2: MD03A1.VIN, U1.VIN
  N31: MD03A1.2PWM, U1.D8
  N32: MD03A1.2INb#142, U1.D11
  N33: MD03A1.2INb#143, U1.D13
  N34: MD03A1.OUT_1A, M1.pin_1
  N35: MD03A1.OUT_1B, M1.pin_2
  N36: MD03A1.OUT_2A, M2.pin_1
  N37: MD03A1.OUT_2B, M2.pin_2
